# Fritzing sketch circuit (saved by Fritzing 0.9.3b)
breadboards: 1

parts:
  DHT11 = Humidity and Temperature Sensor DHT11
  Part1 = LCD1602-I2C
  U1 = NodeMCU V1.0
  M1 = fc-51 [package=THT]

nets (from the schematic view):
  VCC: DHT11.Vcc, Part1.VCC, U1.Vin, M1.pin3
  N1: DHT11.Data-signal, U1.D5
  GND: DHT11.GND_2, Part1.GND, U1.GND, M1.pin1
  N2: Part1.SDA, U1.D2
  N3: Part1.SCL, U1.D1
  N4: U1.A0, M1.pin2

custom parts:
  Humidity and Temperature Sensor DHT11: Digital relative humidity & temperature sensor DHT11
  LCD1602-I2C: A standard character display, usually with 2x16 characters. Comes in many colors with LCM1602 IIC attached.
  NodeMCU V1.0: ESP8266 based NodeMCU
