# Fritzing sketch circuit (saved by Fritzing 0.9.3b)
breadboards: 1

parts:
  U1 = NodeMCU V1.0
  Onderdeel1 = LCD1602-I2C
  DHT1 = Humidity and Temperature Sensor DHT11
  Onderdeel2 = HC-SR501 Body Sensor Module
  S1 = Hall Sensor [part_number=WSH130 package=TO92]
  LED1 = RGB LED (com. anode, rbg) [package="5 mm [THT]"]
  J1 = Power Jack [package=power_jack_pth_lock]

nets:
  N1: U1.D1, Onderdeel1.SCL
  N2: U1.D2, Onderdeel1.SDA
  GND: U1.GND, Onderdeel1.GND, DHT1.GND_2, Onderdeel2.GND, S1.GND, LED1.common_anode, J1.GND
  N3: U1.D5, LED1.red_cathode
  N4: U1.D6, LED1.blue_cathode
  N5: U1.D7, S1.OUT
  N6: U1.D8, LED1.green_cathode
  VCC: U1.Vin, Onderdeel1.VCC, DHT1.Vcc, Onderdeel2.VCC, S1.VCC, J1.PWR
  N7: U1.SD2, DHT1.Data-signal
  N8: U1.SD3, Onderdeel2.OUT

custom parts:
  NodeMCU V1.0: ESP8266 based NodeMCU
  LCD1602-I2C: A standard character display, usually with 2x16 characters. Comes in many colors with LCM1602 IIC attached.
  Humidity and Temperature Sensor DHT11: Digital relative humidity & temperature sensor DHT11
  HC-SR501 Body Sensor Module: Pyroelectric Infrared PIR Motion Sensor Detector Module
  Hall Sensor: A Hall Sensor
